# Fritzing sketch capteurQ (saved by Fritzing 0.9.1b)
breadboards: 1

parts:
  Composant1 = Arduino Nano (Rev3.0)
  U1 = HC-05 Bluetooth Transceiver Breakout Board, 5V, 6pin [package=SIP]
  Composant2 = Gas Sensor Breakout Board

nets:
  GND: Composant1.GND, U1.GND, Composant2.GND
  N1: Composant1.D10, U1.RX
  N2: Composant1.D11/MOSI, U1.TX
  N3: Composant1.A0, Composant2.A1
  3V3: Composant1.3V3, U1.VCC

custom parts:
  HC-05 Bluetooth Transceiver Breakout Board, 5V, 6pin: Breakout board for HC-05 with 5V-to-3V translation, command mode pin (KEY) and STATE pin. http://www.ebay.com/itm/HC-05-Bluetooth-Transceiver-Host-Slave-Master-Module-Wireless-Serial-6pin-/221158958927?pt=LH_DefaultDomain_0&hash=item337e19e74f
